# Fritzing sketch RocketSketch (saved by Fritzing 0.9.3b)
circuit board: 9.27554cm x 5.76152cm
breadboards: 1

parts:
  Componente1 = Arduino Micro (Rev3)
  Antenna1 = HC-12 Antenna
  D1 = Rectifier Diode [package="Melf DO-213 AA [SMD]"]
  Grove_-_AirQuality1 = Grove - Air quality sensor v1.3
  Grove-Acel = Grove 3 Axis Digital Accelerometer 16g
  Grove_-_GPS1 = Grove - GPS
  Grove-Barometer1 = Grove - Barometer (High-Accuracy)
  C1 = Capacitor Polarized [package=cpol-radial-100uf-25v]
  HC-12 = HC-12 Module

nets (from the schematic view):
  GND: Componente1.GND, Grove_-_AirQuality1.GND, Grove-Acel.GND, Grove_-_GPS1.GND, Grove-Barometer1.GND, C1.-, HC-12.GND
  N1: Componente1.D2/SDA, Grove-Acel.SDA, Grove-Barometer1.SDA
  N2: Componente1.D3/SCL, Grove-Acel.SCL, Grove-Barometer1.SCL
  N3: Componente1.D4_PWM/A6, Grove_-_GPS1.TX
  N4: Componente1.D5_PWM, Grove_-_GPS1.RX
  N5: Componente1.D8_PWM/A8, HC-12.RXD
  N6: Componente1.D9_PWM/A9, HC-12.TXD
  VCC: Componente1.5V, D1.anode, Grove_-_AirQuality1.VCC, Grove-Acel.VCC, Grove_-_GPS1.VCC, Grove-Barometer1.VCC, C1.+
  N7: Componente1.A1, Grove_-_AirQuality1.NC
  N8: Componente1.A0, Grove_-_AirQuality1.SIG
  N9: Antenna1.ANT, HC-12.ANT
  N10: D1.cathode, HC-12.VCC

custom parts:
  HC-12 Antenna: Antenna for HC-12 433Mhz Module
  Grove - Air quality sensor v1.3: The sensor is designed for indoor air quality testing. The main gas detected is carbon monoxide, alcohol, acetone, thinner, formaldehyde and other slightly toxic gases. It is compatible with 5V and 3.3V power supply. Features Low power consumption High sensitivity Tiny outline Responsive to a wide scope of target gases Cost efficient Durable Compatible with 5V and 3.3V
  Grove - GPS: This Grove - GPS module is a cost-efficient and field-programmable gadget armed with a SIM28 (U-blox 6 is old version) and serial communication configuration. It features 22 tracking / 66 acquisition channel GPS receiver. The sensitivity of tracking and acquisition both reach up to -160dBm, making it a great choice for personal navigation projects and location services, as well as an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
  Grove - Barometer (High-Accuracy): Barometer (High-Accuracy) Sensor features a HP206C high-accuracy chip to detect barometric pressure ,Altimeter and temperature. It can widely measure pressure ranging from 300mbar~1200mbar, with a super high accuracy of 0.01mbar(0.1m) in ultra-high resolution mode.The chip only accepts 1.8V to 3.6V input voltage. However, with outer circuit added, this module becomes compatible with 3.3V and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
  HC-12 Module: HC-12 433Mhz Module
