# Fritzing sketch luz_temp_sensor (saved by Fritzing 0.9.3b)
circuit board: 8.46667cm x 5.64444cm
breadboards: 1

parts:
  Part1 = Arduino Uno (Rev3)
  R2 = Photocell (LDR) [package=THT]
  T1 = LM35 Temperature Sensor [package="TO92 [THT]"]
  R1 = Resistor [tolerance=±5% resistance=100k package=THT]

nets:
  N1: Part1.A2, T1.Vout
  N2: Part1.A3, R2.pin_1, R1.Pin_0
  N3: Part1.5V, R2.pin_0, T1.+Vs
  GND: Part1.GND, T1.GND, R1.Pin_1
